# Fritzing sketch hit_the_light (saved by Fritzing 0.9.3b)
breadboards: 1

parts:
  Part1 = Arduino Uno (Rev3)
  R1 = Resistor [tolerance=±5% resistance=220 package=THT]  # not connected
  LED1 = LED - 5mm [color="Green (560nm)" package="5 mm [THT]"]  # not connected
  S1 = Pushbutton [package="[THT]"]
  R2 = Resistor [tolerance=±5% resistance=10k package=THT]
  LED2 = LED - 5mm [color="Green (560nm)" package="5 mm [THT]"]  # not connected
  R3 = Resistor [tolerance=±5% resistance=220 package=THT]  # not connected
  LED3 = LED - 5mm [color="Green (560nm)" package="5 mm [THT]"]  # not connected
  R4 = Resistor [tolerance=±5% resistance=220 package=THT]  # not connected
  S2 = Pushbutton [package="[THT]"]  # not connected
  S3 = Pushbutton [package="[THT]"]  # not connected
  R5 = Resistor [tolerance=±5% resistance=10k package=THT]
  R6 = Resistor [tolerance=±5% resistance=10k package=THT]
  LED4 = LED - 5mm [color="White (6500K)" package="5 mm [THT]"]
  R7 = Resistor [tolerance=±5% resistance=220 package=THT]
  R8 = Rotary Potentiometer (Small) [maximum_resistance=100kΩ package=THT]

nets:
  N1: Part1.A0, R8.wiper
  N2: Part1.D8, R5.Pin_1
  N3: Part1.D9_PWM, R6.Pin_1
  N4: Part1.D3_PWM, R7.Pin_1
  N5: Part1.D7, R2.Pin_1
  N6: Part1.5V, S1.Pin_1, S1.Pin_2, S1.Pin_3, S1.Pin_4, R8.leg2
  N7: Part1.GND, R2.Pin_0, R5.Pin_0, R6.Pin_0, LED4.cathode, R8.leg1
  N8: LED4.anode, R7.Pin_0
