# Fritzing sketch smart_toilet (saved by Fritzing 0.9.3b)
breadboards: 1

parts:
  LED1 = LED - 5mm [color="Green (555nm)" package="5 mm [THT]"]
  S2 = Pushbutton [package="[THT]"]
  LED2 = LED - 5mm [color="Green (555nm)" package="5 mm [THT]"]
  LED3 = LED - 5mm [color="Red (633nm)" package="5 mm [THT]"]
  R1 = Resistor [tolerance=±5% resistance=220 package=THT]
  R2 = Resistor [tolerance=±5% resistance=220 package=THT]
  R3 = Resistor [tolerance=±5% resistance=220 package=THT]
  hc-sr1 = hc-sr04
  PIR2 = PIR sensor
  Componente1 = Arduino Nano (Rev3.0) (ICSP)
  S3 = Pushbutton [package="[THT]"]

nets:
  GND: LED1.cathode, S2.Pin_3, S2.Pin_4, LED2.cathode, LED3.cathode, hc-sr1.GND, PIR2.GND, Componente1.GND, S3.Pin_3, S3.Pin_4
  N1: LED1.anode, R1.Pin_1
  N2: S2.Pin_1, S2.Pin_2, Componente1.D3
  N3: LED2.anode, R2.Pin_1
  N4: LED3.anode, R3.Pin_1
  N5: R1.Pin_0, Componente1.D4
  N6: R2.Pin_0, Componente1.D5
  N7: R3.Pin_0, Componente1.D6
  VCC: hc-sr1.VCC, PIR2.VDD, Componente1.5V
  N8: hc-sr1.Trig, Componente1.D8
  N9: hc-sr1.Echo, Componente1.D9
  N10: PIR2.SIG, Componente1.D7
  N11: Componente1.D2, S3.Pin_1, S3.Pin_2
