# Fritzing sketch event_tracker (saved by Fritzing 0.9.3b)
breadboards: 1

parts:
  Raspberry_Pi_1 = Raspberry Pi 3 [part_number=RPI-3-V1.2]
  Componente1 = Arduino Uno (Rev3)
  Componente2 = Bluetooth HC-05 Macho
  PIR1 = PIR sensor
  Part1 = KY-015 Temperature & Humidity Sensor Module [package="Breakout board"]
  LED1 = LED - 5mm [color="Red (633nm)" package="5 mm [THT]"]
  R1 = Resistor [tolerance=±5% resistance=220 package=THT]
  LED2 = LED - 5mm [color="Red (633nm)" package="5 mm [THT]"]
  LED3 = LED - 5mm [color="Green (560nm)" package="5 mm [THT]"]
  LED4 = LED - 5mm [color="Blue (470nm)" package="5 mm [THT]"]
  S1 = Momentary Switch [package=ksa_sealed_tac_switch]

nets:
  3V3: Raspberry_Pi_1.3v3, Componente2.VCC, S1.3, S1.4
  N1: Raspberry_Pi_1.GPIO17, S1.1, S1.2
  N2: Raspberry_Pi_1.GPIO22, LED2.anode
  N3: Raspberry_Pi_1.GPIO23, LED3.anode
  N4: Raspberry_Pi_1.GPIO18, LED4.anode
  GND: Raspberry_Pi_1.GND, Componente2.GND, LED2.cathode, LED3.cathode, LED4.cathode
  N5: Componente1.D3_PWM, PIR1.SIG
  N6: Componente1.D7, Part1.Vin
  5V: Componente1.5V, PIR1.VDD, Part1.S
  GND_2: Componente1.GND, PIR1.GND, Part1.-, LED1.cathode
  N7: LED1.anode, R1.Pin_1

notes:
  Cavo USB
  L1
  L2
  L3

custom parts:
  KY-015 Temperature & Humidity Sensor Module: KY-015 temperature and humidity sensor module, provides a low-latency serial interface to measure humidity and temperature.
